// Logisim project adh0.circ as structural Verilog
module ALU (
  input  [2:0] op,
  input  [7:0] x,
  input  [7:0] y,
  output [7:0] z
);

  wire n7404_1_pin2, n7404_1_pin4, n7404_1_pin6, n7404_1_pin8, n7404_1_pin10, n7404_1_pin12, n7432_1_pin8,
       n7442_1_pin2, n7442_1_pin3, n7442_1_pin4, n7442_1_pin5, n7442_1_pin6, n7442_1_pin7, n7442_1_pin12,
       n7486_1_pin2, n74283_1_pin7;
  wire [7:0] n7486_1_pin11;

  _7442 u_7442_1 (
    .pin2(n7442_1_pin2), .pin3(n7442_1_pin3), .pin4(n7442_1_pin4), .pin5(n7442_1_pin5), .pin6(n7442_1_pin6),
    .pin7(n7442_1_pin7), .pin15(op[0]), .pin14(op[1]), .pin13(op[2]), .pin12(n7442_1_pin12));  // open: pin1, pin11, pin10, pin9
  _7404 u_7404_1 (
    .pin1(n7442_1_pin5), .pin2(n7404_1_pin2), .pin3(n7442_1_pin6), .pin4(n7404_1_pin4), .pin5(n7442_1_pin7),
    .pin6(n7404_1_pin6), .pin13(n7442_1_pin2), .pin12(n7404_1_pin12), .pin11(n7442_1_pin3),
    .pin10(n7404_1_pin10), .pin9(n7442_1_pin4), .pin8(n7404_1_pin8));
  _7486 u_7486_1 (
    .pin1(y[4]), .pin2(n7486_1_pin2), .pin3(n7486_1_pin11[4]), .pin4(y[5]), .pin5(n7486_1_pin2),
    .pin6(n7486_1_pin11[5]), .pin13(y[0]), .pin12(n7486_1_pin2), .pin11(n7486_1_pin11[0]), .pin10(y[1]),
    .pin9(n7486_1_pin2), .pin8(n7486_1_pin11[1]));
  _7432 u_7432_1 (
    .pin13(n7404_1_pin8), .pin12(n7404_1_pin10), .pin11(n7486_1_pin2), .pin10(n7404_1_pin10),
    .pin9(n7404_1_pin12), .pin8(n7432_1_pin8));  // open: pin1, pin2, pin3, pin4, pin5, pin6
  _7486 u_7486_2 (
    .pin1(y[6]), .pin2(n7486_1_pin2), .pin3(n7486_1_pin11[6]), .pin4(y[7]), .pin5(n7486_1_pin2),
    .pin6(n7486_1_pin11[7]), .pin13(y[2]), .pin12(n7486_1_pin2), .pin11(n7486_1_pin11[2]), .pin10(y[3]),
    .pin9(n7486_1_pin2), .pin8(n7486_1_pin11[3]));
  _74283 u_74283_1 (
    .pin1(z[5]), .pin2(n7486_1_pin11[5]), .pin3(x[5]), .pin4(z[4]), .pin5(x[4]), .pin6(n7486_1_pin11[4]),
    .pin7(n74283_1_pin7), .pin15(n7486_1_pin11[6]), .pin14(x[6]), .pin13(z[6]), .pin12(x[7]),
    .pin11(n7486_1_pin11[7]), .pin10(z[7]));  // open: pin9
  _74283 u_74283_2 (
    .pin1(z[1]), .pin2(n7486_1_pin11[1]), .pin3(x[1]), .pin4(z[0]), .pin5(x[0]), .pin6(n7486_1_pin11[0]),
    .pin7(n7432_1_pin8), .pin15(n7486_1_pin11[2]), .pin14(x[2]), .pin13(z[2]), .pin12(x[3]),
    .pin11(n7486_1_pin11[3]), .pin10(z[3]), .pin9(n74283_1_pin7));
  // also tied to GND on the sheet: n7442_1_pin12
endmodule
